// Logisim project LogicDesign_Lab02.circ as structural Verilog
module Half_Adder (
  input  in_1,
  input  in_2,
  output out_3,
  output out_4
);

  wire and_1_out, xor_1_out;

  xor xor_1 (xor_1_out, in_1, in_2);
  and and_1 (and_1_out, in_1, in_2);
endmodule

module Full_Adder (
  input  in_1,
  input  in_2,
  input  in_3,
  input  in_4,
  output out_5,
  output out_6
);

  wire and_1_out, and_2_out, or_1_out, xor_1_out, xor_2_out;

  xor xor_1 (xor_1_out, in_1, in_3);
  and and_1 (and_1_out, in_1, in_3);
  xor xor_2 (xor_2_out, xor_1_out, in_4);
  and and_2 (and_2_out, xor_1_out, in_4);
  or or_1 (or_1_out, and_1_out, and_2_out);
endmodule

module Adder_Subtractor_4bit (
  input  in_1,
  input  in_2,
  input  in_3,
  output out_4,
  output out_5
);

  wire and_1_out, and_2_out, or_1_out, xor_1_out;

  xor xor_1 (xor_1_out, in_1, in_2);
  and and_1 (and_1_out, xor_1_out, in_3);
  buf and_2 (and_2_out, in_2);  // AND_Gate
  or or_1 (or_1_out, xor_1_out, and_1_out);
endmodule
