// Logisim project XOR_from_basic_gates.circ as structural Verilog
module AND_Gate (
  input  in_1,
  input  in_2
);

  wire and_1_out, not_1_out, undriven, undriven_2;

  not not_1 (not_1_out, undriven);
  not not_2 (not_1_out, undriven_2);
  // AND_Gate_part and_1 has open pins: out=and_1_out
  // AND_Gate_part and_2 has open pins: out=and_1_out
  // OR_Gate or_1 is placed but not wired
endmodule
